// Logisim project IA60MIPS.circ as structural Verilog: 3 circuits, main circuit MIPS
module MIPS (
);

  wire ALU, ALUB, and_1_out, and_2_out, and_3_out, and_4_out, and_5_out, ANDI, BEQ, BGTZ, BLEZ, BNE, clk,
       clock_1_out, comparator_1_eq, comparator_1_gt, comparator_1_lt, control_alu_1_p3, HALT, JAL, JR,
       MRead, MWrite, or_1_out, Reg, register_file_1_p6, RegWrite, RSUBLT, Zero;
  wire [1:0] Dest, J, RegData;
  wire [2:0] OPALU;
  wire [4:0] multiplexer_4_out, multiplexer_5_out, multiplexer_6_out;
  wire [5:0] OPCO;
  wire [15:0] Desplazamiento;
  wire [25:16] dir;
  wire [27:0] PC_4;
  wire [31:0] adder_2_out, bit_extender_1_out, bit_extender_2_out, DesplExten, Direccion, MData,
       multiplexer_1_out, multiplexer_3_out, multiplexer_7_out, PC_q, RALU, Reg1, Reg2, Shift;
  wire [31:28] \new ;

  Clock #(.highDuration(16), .lowDuration(16)) clock_1 (.out(clock_1_out));
  // Probe on multiplexer_1_out
  Multiplexer #(.select(2), .width(32), .enable("false")) multiplexer_1 (
    .in0(Direccion), .in1({\new , dir, Desplazamiento, 2'b00}), .in2(Reg1), .out(multiplexer_1_out), .sel(J));  // open: in3
  assign bit_extender_1_out = {{16{Desplazamiento[15]}}, Desplazamiento};  // Bit_Extender bit_extender_1
  assign bit_extender_2_out = {{16{1'b0}}, Desplazamiento};  // Bit_Extender bit_extender_2
  Register #(.width(32)) PC (.D(multiplexer_1_out), .Q(PC_q), .clk(clk));  // open: en, clr
  Multiplexer #(.width(32), .enable("false")) multiplexer_2 (
    .in0(bit_extender_1_out), .in1(bit_extender_2_out), .out(DesplExten), .sel(ANDI));
  // ClockGen clockgen_1: pin names not known; wires that end beside it: HALT, clock_1_out, clk
  Adder #(.width(32)) adder_1 (.a(32'h4), .b(PC_q), .out({\new , PC_4}));  // open: cin, cout
  // Instruction_memory instruction_memory_1: pin names not known; wires that end beside it: PC_q, {OPCO, dir, Desplazamiento}
  // Probe on DesplExten
  // Probe on {OPCO, dir, Desplazamiento}
  Multiplexer #(.width(32), .enable("false")) multiplexer_3 (
    .in0(DesplExten), .in1(Reg2), .out(multiplexer_3_out), .sel(ALUB));
  // Probe on OPCO
  // Probe on {OPCO, dir, Desplazamiento}
  // Probe on {OPCO, dir, Desplazamiento}
  // Control_ALU control_alu_1: pin names not known; wires that end beside it: OPALU, Desplazamiento[5:0], control_alu_1_p3
  // ALU alu_1: pin names not known; wires that end beside it: Reg1, multiplexer_3_out, control_alu_1_p3, Zero, RALU
  Shifter #(.width(32)) shifter_1 (.in(DesplExten), .\dist (5'b00010), .out(Shift));
  // Probe on control_alu_1_p3
  // Probe on RALU
  UCO uco_1 (
    .J(J), .HALT(HALT), .RegWrite(RegWrite), .MWrite(MWrite), .MRead(MRead), .ALU(ALU), .OPALU(OPALU),
    .Dest(Dest), .ALUB(ALUB), .RData(RegData), .BEQ(BEQ), .ANDI(ANDI), .BNE(BNE), .OPCO(OPCO), .BGTZ(BGTZ),
    .BLEZ(BLEZ), .Reg(Reg), .JAL(JAL), .JR(JR), .Funcion(Desplazamiento[5:0]), .RSUBLT(RSUBLT));
  // Data_Memory_32 data_memory_32_1: pin names not known; wires that end beside it: RALU, Reg2, clk, MRead, MWrite, MData
  Multiplexer #(.width(5), .enable("false")) multiplexer_4 (
    .in0(dir[20:16]), .in1(dir[25:21]), .out(multiplexer_4_out), .sel(Reg));
  Multiplexer #(.select(2), .width(5), .enable("false")) multiplexer_5 (
    .in0(dir[20:16]), .in1(Desplazamiento[15:11]), .in2({5{1'b1}}), .out(multiplexer_5_out), .sel(Dest));  // open: in3
  Comparator #(.width(32)) comparator_1 (
    .a(Reg1), .b(Reg2), .gt(comparator_1_gt), .eq(comparator_1_eq), .lt(comparator_1_lt));
  Multiplexer #(.width(5), .enable("false")) multiplexer_6 (
    .in0(dir[25:21]), .in1(dir[20:16]), .out(multiplexer_6_out), .sel(Reg));
  Adder #(.width(32)) adder_2 (.a({\new , PC_4}), .b(Shift), .out(adder_2_out));  // open: cin, cout
  Multiplexer #(.select(2), .width(32), .enable("false")) multiplexer_7 (
    .in0(MData), .in1(RALU), .in2({Desplazamiento, {16{1'b0}}}), .in3({\new , PC_4}),
    .out(multiplexer_7_out), .sel(RegData));
  Multiplexer #(.width(32), .enable("false")) multiplexer_8 (
    .in0({\new , PC_4}), .in1(adder_2_out), .out(Direccion), .sel(or_1_out));
  or or_1 (or_1_out, and_2_out, and_3_out, and_4_out, and_5_out);
  // Register_file register_file_1: pin names not known; wires that end beside it: multiplexer_6_out, multiplexer_4_out, multiplexer_5_out, multiplexer_7_out, clk, register_file_1_p6, Reg1, Reg2
  or or_2 (register_file_1_p6, RegWrite, and_1_out);
  and and_1 (and_1_out, comparator_1_gt, RSUBLT);
  and and_2 (and_2_out, Zero, BEQ);
  and and_3 (and_3_out, ~Zero, BNE);  // AND_Gate
  and and_4 (and_4_out, BGTZ, RALU[0]);
  and and_5 (and_5_out, BLEZ, ~RALU[0]);  // AND_Gate

  // Other names for the same wires on the sheet: new[27:2] = {dir, Desplazamiento}; rt[4:0] = dir[20:16];
  //   rs[4:0] = dir[25:21]; dir[15:0] = Desplazamiento; Funcion[5:0] = Desplazamiento[5:0];
  //   InmDespl[31:16] = Desplazamiento; rd[4:0] = Desplazamiento[15:11]; PC_4[31:28] = \new ; RALU1b = RALU[0]
endmodule

module UCO (
  input  [5:0] Funcion,
  input  [5:0] OPCO,
  output [1:0] J,
  output HALT,
  output ALU,
  output BEQ,
  output ANDI,
  output BNE,
  output BGTZ,
  output BLEZ,
  output JAL,
  output JR,
  output RSUBLT,
  output MWrite,
  output [1:0] Dest,
  output ALUB,
  output [1:0] RData,
  output Reg,
  output RegWrite,
  output MRead,
  output [2:0] OPALU
);

  wire decoder_uco_1_addi, decoder_uco_1_andi, decoder_uco_1_j, decoder_uco_1_lui, decoder_uco_1_ori;

  Decoder_UCO decoder_uco_1 (
    .J(decoder_uco_1_j), .OPCO(OPCO), .HALT(HALT), .LW(MRead), .SW(MWrite), .ALU(ALU),
    .ADDI(decoder_uco_1_addi), .BEQ(BEQ), .ANDI(decoder_uco_1_andi), .LUI(decoder_uco_1_lui),
    .ORI(decoder_uco_1_ori), .BNE(BNE), .BGTZ(BGTZ), .BLEZ(BLEZ), .JAL(Dest[1]), .JRbit(Funcion), .JR(J[1]),
    .RSUBLT(RSUBLT));
  or or_1 (RegWrite, MRead, ALU, decoder_uco_1_addi, decoder_uco_1_andi, decoder_uco_1_lui, decoder_uco_1_ori, Dest[1]);
  or or_2 (OPALU[2], ALU, BGTZ, BLEZ);
  or or_3 (OPALU[1], ALU, decoder_uco_1_andi, decoder_uco_1_ori);
  or or_4 (OPALU[0], ALU, BEQ, decoder_uco_1_ori, BNE, RSUBLT);
  or or_5 (ALUB, ALU, BEQ, BNE, BGTZ, BLEZ, RSUBLT);
  or or_6 (RData[1], decoder_uco_1_lui, Dest[1]);
  or or_7 (RData[0], ALU, decoder_uco_1_addi, decoder_uco_1_andi, decoder_uco_1_ori, Dest[1], RSUBLT);
  or or_8 (Reg, BGTZ, RSUBLT, BLEZ);
  or or_9 (J[0], decoder_uco_1_j, Dest[1]);
  // Probe on MRead
  // Probe on MWrite
  // Probe on decoder_uco_1_addi
  or or_10 (ANDI, decoder_uco_1_andi, decoder_uco_1_ori);
  // Probe on decoder_uco_1_lui
  // Probe on decoder_uco_1_ori

  assign Dest[0] = ALU;
  assign JAL = Dest[1];
  assign JR = J[1];
endmodule

module Decoder_UCO (
  input  [5:0] OPCO,
  input  [5:0] JRbit,
  output J,
  output JR,
  output HALT,
  output RSUBLT,
  output LW,
  output JAL,
  output ALU,
  output SW,
  output BLEZ,
  output ADDI,
  output BEQ,
  output ANDI,
  output LUI,
  output ORI,
  output BNE,
  output BGTZ
);

  wire ALU_2_out, ALU_out, and_4_out;

  and u_J (J, ~OPCO[0], OPCO[1], ~OPCO[2], ~OPCO[3], ~OPCO[4], ~OPCO[5]);  // AND_Gate
  and u_HALT (HALT, OPCO[0], OPCO[1], OPCO[2], OPCO[3], OPCO[4], OPCO[5]);
  and u_LW (LW, OPCO[0], OPCO[1], ~OPCO[2], ~OPCO[3], ~OPCO[4], OPCO[5]);  // AND_Gate
  and u_SW (SW, OPCO[0], OPCO[1], ~OPCO[2], OPCO[3], ~OPCO[4], OPCO[5]);  // AND_Gate
  and u_ALU (ALU_out, ~OPCO[0], ~OPCO[1], ~OPCO[2], ~OPCO[3], ~OPCO[4], ~OPCO[5]);  // AND_Gate
  and u_ADDI (ADDI, ~OPCO[5], ~OPCO[4], OPCO[3], ~OPCO[2], ~OPCO[1], ~OPCO[0]);  // AND_Gate
  and and_1 (ALU, ALU_out, ~and_4_out);  // AND_Gate
  and u_BEQ (BEQ, ~OPCO[5], ~OPCO[4], ~OPCO[3], OPCO[2], ~OPCO[1], ~OPCO[0]);  // AND_Gate
  and and_2 (RSUBLT, OPCO[5], ~OPCO[4], OPCO[3], ~OPCO[2], OPCO[1], ~OPCO[0]);  // AND_Gate
  and u_ANDI (ANDI, ~OPCO[5], ~OPCO[4], OPCO[3], OPCO[2], ~OPCO[1], ~OPCO[0]);  // AND_Gate
  and u_LUI (LUI, ~OPCO[5], ~OPCO[4], OPCO[3], OPCO[2], OPCO[1], OPCO[0]);  // AND_Gate
  and and_3 (JR, ALU_2_out, and_4_out);
  and u_ORI (ORI, ~OPCO[5], ~OPCO[4], OPCO[3], OPCO[2], ~OPCO[1], OPCO[0]);  // AND_Gate
  and and_4 (and_4_out, ~JRbit[5], ~JRbit[4], JRbit[3], ~JRbit[2], ~JRbit[1], ~JRbit[0]);  // AND_Gate
  and u_BNE (BNE, ~OPCO[5], ~OPCO[4], ~OPCO[3], OPCO[2], ~OPCO[1], OPCO[0]);  // AND_Gate
  and ALU_2 (ALU_2_out, ~OPCO[0], ~OPCO[1], ~OPCO[2], ~OPCO[3], ~OPCO[4], ~OPCO[5]);  // AND_Gate
  and u_JAL (JAL, OPCO[0], OPCO[1], ~OPCO[2], ~OPCO[3], ~OPCO[4], ~OPCO[5]);  // AND_Gate
  and u_BLEZ (BLEZ, ~OPCO[0], OPCO[1], OPCO[2], ~OPCO[3], ~OPCO[4], ~OPCO[5]);  // AND_Gate
  and u_BGTZ (BGTZ, OPCO[0], OPCO[1], OPCO[2], ~OPCO[3], ~OPCO[4], ~OPCO[5]);  // AND_Gate
endmodule
